# Fritzing sketch connection-diagram (saved by Fritzing 0.9.2b)
circuit board: 3.85576cm x 6.90464cm
breadboards: 1

parts:
  R5 = Resistor [tolerance=±5% resistance=100 package=THT]
  R7 = Resistor [tolerance=±5% resistance=1k package=THT]
  R8 = Resistor [tolerance=±5% resistance=1k package=THT]
  R9 = Resistor [tolerance=±5% resistance=1k package=THT]
  JP2 = Header 3 [package=molex-1x3_lock]
  JP3 = Header 2 [package=molex-1x2_lock]
  JP4 = Header 2 [package=molex-1x2_lock]
  R10 = Resistor [tolerance=±5% resistance=1k package=THT]
  J2 = male pin header, 2 pins [form="♂ (male)"]
  Bauteil1 = Arduino Nano (Rev3.0)
  M1 = Stepper Motor - Bipolar
  R6 = Resistor [tolerance=±5% resistance=1k package=THT]
  C4 = Electrolytic Capacitor [capacitance=0.1mF package="100 mil [THT, electrolytic]"]
  JP9 = Header 2 [package=jst-2-pth]
  MD09B2 = A4988 Stepper Motor Driver Carrier

nets:
  N1: R5.Pin_0, J2.pin1
  5V: R5.Pin_1, JP2.1, R10.Pin_0, Bauteil1.5V, MD09B2.VDD
  N2: R7.Pin_0, JP3.2, Bauteil1.D9
  N3: R7.Pin_1, R8.Pin_1, R9.Pin_1, JP4.2, Bauteil1.GND, R6.Pin_1, MD09B2.GROUND#147
  N4: R8.Pin_0, JP2.2, Bauteil1.D12/MISO
  N5: R9.Pin_0, JP2.3, Bauteil1.D11/MOSI
  N6: JP3.1, Bauteil1.D10, R6.Pin_0
  N7: JP4.1, R10.Pin_1, Bauteil1.D8
  N8: J2.pin2, Bauteil1.RESET
  N9: Bauteil1.D2, MD09B2.RESET
  N10: Bauteil1.D3, MD09B2.MS3
  N11: Bauteil1.D4, MD09B2.MS1
  N12: Bauteil1.D5, MD09B2.MS2
  N13: Bauteil1.D6, MD09B2.Enable
  N14: Bauteil1.A2, MD09B2.SLEEP
  N15: Bauteil1.A1, MD09B2.STEP
  N16: Bauteil1.A0, MD09B2.DIR
  N17: M1.A, MD09B2.OUT_2B
  N18: M1.C, MD09B2.OUT_2A
  N19: M1.B, MD09B2.OUT_1A
  N20: M1.D, MD09B2.OUT_1B
  N21: C4.-, JP9.2, MD09B2.GROUND#141
  N22: C4.+, JP9.1, MD09B2.VMOT

notes:
  Motor
  120Ω
  1kΩ
  Switch
  Sensor
  100µF
  Autoreset
  Arduino Nano
  Pololu DRV8825
  12V
  DC
  STEP
  RESET
  SLEEP
  DIR
  MS3
  1A
  1B
  VDD
  GND
  MS2
  MS1
  ENABL
  2B
  2A
  VMOT
  For questions, code, etc. contact
  johann.jacobsohn@uni-hamburg.de
  D7

custom parts:
  A4988 Stepper Motor Driver Carrier: The Pololu stepper motor driver carrier for the A4988 motor driver integrated circuits. http://www.pololu.com/catalog/product/1182
